# Fritzing sketch Debounce Switch 3 (saved by Fritzing 0.9.0b)
breadboards: 1

parts:
  R1 = Resistor [resistance=220 tolerance=±5% package=THT]
  R2 = Resistor [resistance=220 tolerance=±5% package=THT]
  S1 = Pushbutton [package="[THT]"]
  R3 = Resistor [resistance=220 tolerance=±5% package=THT]
  LED3 = LED - 5mm [color="Yellow (585nm)" package="5 mm [THT]"]
  LED1 = LED - 5mm [color="Red (633nm)" package="5 mm [THT]"]
  Arduino1 = Arduino Uno (Rev3)

nets:
  N1: R1.Pin_0, LED1.anode
  N2: R2.Pin_1, LED3.anode
  N3: S1.Pin_1, S1.Pin_2, R3.Pin_0, Arduino1.D2
  N4: S1.Pin_3, S1.Pin_4
  N5: R3.Pin_1, Arduino1.GND
  N6: LED3.cathode, LED1.cathode
