# Fritzing sketch alarma prototipo 1 (saved by Fritzing 0.9.0b)
breadboards: 2

parts:
  IC1 = DIP - 14 pins [chip_label=74LS11 package="DIP (Dual Inline) [THT]"]
  U1 = 74HC4051 [package=so16]
  Parte1 = Arduino Leonardo (Rev3b)
  B2 = Pushbutton [package="[THT]"]
  R1 = Resistor [tolerance=±5% resistance=220 package=THT]
  B1 = Pushbutton [package="[THT]"]
  R2 = Resistor [tolerance=±5% resistance=220 package=THT]
  B3 = Pushbutton [package="[THT]"]
  R3 = Resistor [tolerance=±5% resistance=220 package=THT]
  LED1 = smd LED [color="Red (633nm)" package="1206 [SMD]"]
  S1 = Pushbutton [package="[THT]"]
  S2 = Pushbutton [package="[THT]"]
  S3 = Pushbutton [package="[THT]"]
  S4 = Pushbutton [package="[THT]"]
  S5 = Pushbutton [package="[THT]"]
  R7 = Resistor [package="2010 [SMD]"]
  R9 = Resistor [tolerance=±5% resistance=1k package="1206 [SMD]"]
  R5 = Resistor [tolerance=±5% resistance=2.2k package=THT]
  R4 = Resistor [tolerance=±5% resistance=47k package=THT]
  R6 = Resistor [tolerance=±5% resistance=680 package=THT]
  R8 = Resistor [tolerance=±5% resistance=390 package=THT]
  U5 = LCD-16X2 [package=lcd-16x2_nosilk]
  KEYPAD1 = Membrane Matrix Keypad
  LED2 = smd LED [color="Red (633nm)" package="0805 [SMD]"]
  LED3 = smd LED [color="Red (633nm)" package="0805 [SMD]"]
  R10 = Resistor [tolerance=±5% resistance=220 package="0603 [SMD]"]
  R11 = Resistor [tolerance=±5% resistance=220 package=THT]  # not connected

nets:
  GND: IC1.GND, U1.INH, U1.VEE, U1.VSS, Parte1.GND, B2.Pin_3, B2.Pin_4, B1.Pin_4, B3.Pin_3, B3.Pin_4, LED1.cathode, R9.Pin_1, U5.DB6, R10.Pin_1
  N1: IC1.Y3, Parte1.D0/RX
  N2: IC1.A3, U1.IO3, B3.Pin_1, B3.Pin_2, R3.Pin_1
  N3: IC1.B3, U1.IO2, B2.Pin_1, B2.Pin_2, R1.Pin_1
  N4: IC1.C3, U1.IO1, B1.Pin_2, R2.Pin_1
  VCC: IC1.VCC, U1.VDD, Parte1.5V, R1.Pin_0, R2.Pin_0, R3.Pin_0, R7.Pin_0, U5.DB7
  N5: U1.IO, Parte1.D12/A11
  N6: U1.C, Parte1.A2
  N7: U1.B, Parte1.A1
  N8: U1.A, Parte1.A0
  N9: Parte1.D4/A6, KEYPAD1.7
  N10: Parte1.D5_PWM, KEYPAD1.6
  N11: Parte1.D6_PWM/A7, KEYPAD1.5
  N12: Parte1.D7, KEYPAD1.4
  N13: Parte1.A3, LED3.anode
  N14: Parte1.A4, LED2.anode
  N15: Parte1.A5, S1.Pin_1, S1.Pin_2, S2.Pin_1, S2.Pin_2, S3.Pin_1, S3.Pin_2, S4.Pin_1, S4.Pin_2, S5.Pin_1, S5.Pin_2, R9.Pin_0
  N16: Parte1.D13_PWM, LED1.anode
  N17: Parte1.SDA, U5.A
  N18: Parte1.SCL, U5.K
  N19: S1.Pin_3, S1.Pin_4, R8.Pin_0
  N20: S2.Pin_3, S2.Pin_4, R7.Pin_1
  N21: S3.Pin_3, S3.Pin_4, R6.Pin_0
  N22: S4.Pin_3, S4.Pin_4, R5.Pin_0
  N23: S5.Pin_3, S5.Pin_4, R4.Pin_0
  N24: R5.Pin_1, R4.Pin_1, R6.Pin_1, R8.Pin_1
  N25: LED3.cathode, R10.Pin_0

custom parts:
  DIP - 14 pins: A DIP stand-in part for whatever IC you want. With 14 pins on a 300mil dual inline package (DIP) footprint.
  Membrane Matrix Keypad: Membrane Matrix 3x4 Keypad
